// Logisim project S2-T-16.circ as structural Verilog: 3 circuits, main circuit main
// 3-input comparator
module comparator_server (
  input  [3:0] Server_1_counter,
  input  [3:0] Server_2_counter,
  input  [3:0] Server_3_counter,
  output Server_1,
  output Server_2,
  output Server_3
);

  wire comparator_1_eq, comparator_1_gt, comparator_1_lt, comparator_2_eq, comparator_2_gt, comparator_2_lt,
       comparator_3_eq, comparator_3_gt, comparator_3_lt, or_1_out, or_2_out, or_3_out;

  Comparator #(.width(4), .mode("unsigned")) comparator_1 (
    .a(Server_1_counter), .b(Server_2_counter), .gt(comparator_1_gt), .eq(comparator_1_eq),
    .lt(comparator_1_lt));
  Comparator #(.width(4), .mode("unsigned")) comparator_2 (
    .a(Server_1_counter), .b(Server_3_counter), .gt(comparator_2_gt), .eq(comparator_2_eq),
    .lt(comparator_2_lt));
  Comparator #(.width(4), .mode("unsigned")) comparator_3 (
    .a(Server_2_counter), .b(Server_3_counter), .gt(comparator_3_gt), .eq(comparator_3_eq),
    .lt(comparator_3_lt));
  or or_1 (or_1_out, comparator_1_eq, comparator_1_lt);
  or or_2 (or_2_out, comparator_2_eq, comparator_2_lt);
  or or_3 (or_3_out, comparator_3_eq, comparator_3_lt);
  and and_1 (Server_1, or_1_out, or_2_out);
  and and_2 (Server_2, comparator_1_gt, or_3_out);
  and and_3 (Server_3, comparator_2_gt, comparator_3_gt);

  // Notes on the sheet:
  //   Description:
  //   ->This 3-Input comparator is used to compare three 4-bit input and gives the input with least  count.
  //   3-Input 4-bit Comparator 
endmodule

module main (
  input  [7:0] Task_input_Queue,
  input  in_2,
  input  [3:0] in_3,
  input  [3:0] in_4,
  input  [3:0] in_5,
  input  [3:0] in_6,
  input  [3:0] in_7,
  input  [3:0] in_8,
  output out_9,
  output [2:0] out_10
);

  wire and_1_out, and_4_out, and_5_out, and_6_out, and_7_out, and_9_out, and_10_out, Clock_out,
       comparator_1_eq, comparator_1_gt, comparator_2_eq, comparator_2_gt, comparator_3_eq, comparator_3_gt,
       comparator_server_1_server_1, comparator_server_1_server_2, comparator_server_1_server_3,
       multiplexer_1_out, not_1_out, not_3_out, or_1_out, or_2_out, or_4_out, or_5_out, or_6_out, or_7_out,
       priority_encoder_1_gs, Reset_out;
  wire [3:0] adder_1_out, adder_2_out, adder_3_out, s1_q, s2_q, s3_q;
  wire [7:0] and_2_out, and_3_out, and_8_out, decoder_1_out0, n8_input_flip_flop_1_output,
       n8_input_flip_flop_2_output, nand_1_out, not_2_out, or_3_out;

  Button Clock (.out(Clock_out));
  Button Reset (.out(Reset_out));
  or or_1 (or_1_out, n8_input_flip_flop_2_output[0], n8_input_flip_flop_2_output[1], n8_input_flip_flop_2_output[2], n8_input_flip_flop_2_output[3], n8_input_flip_flop_2_output[4], n8_input_flip_flop_2_output[5], n8_input_flip_flop_2_output[6], n8_input_flip_flop_2_output[7]);
  _8_input_flip_flop u_8_input_flip_flop_1 (
    .\input (Task_input_Queue), .clk(and_1_out), .clear__1_to_clear(not_1_out),
    .\output (n8_input_flip_flop_1_output));
  not not_1 (not_1_out, or_1_out);
  and and_1 (and_1_out, or_2_out, Clock_out);
  or or_2 (or_2_out, and_8_out[0], and_8_out[1], and_8_out[2], and_8_out[3], and_8_out[4], and_8_out[5], and_8_out[6], and_8_out[7]);
  assign nand_1_out = ~(Task_input_Queue & n8_input_flip_flop_1_output);  // NAND_Gate nand_1, 8 bits wide
  assign and_2_out = Task_input_Queue & nand_1_out;  // AND_Gate and_2, 8 bits wide
  assign or_3_out = and_2_out | n8_input_flip_flop_2_output;  // OR_Gate or_3, 8 bits wide
  assign and_3_out = or_3_out & Task_input_Queue;  // AND_Gate and_3, 8 bits wide
  and and_4 (and_4_out, and_7_out, and_10_out);
  and and_5 (and_5_out, and_7_out, comparator_server_1_server_2);
  and and_6 (and_6_out, and_7_out, comparator_server_1_server_3);
  Decoder #(.select(3)) decoder_1 (
    .out0(decoder_1_out0[0]), .out1(decoder_1_out0[1]), .out2(decoder_1_out0[2]), .out3(decoder_1_out0[3]),
    .out4(decoder_1_out0[4]), .out5(decoder_1_out0[5]), .out6(decoder_1_out0[6]), .out7(decoder_1_out0[7]),
    .sel(out_10));  // open: en
  Priority_Encoder priority_encoder_1 (
    .in0(and_3_out[0]), .in1(and_3_out[1]), .in2(and_3_out[2]), .in3(and_3_out[3]), .in4(and_3_out[4]),
    .in5(and_3_out[5]), .in6(and_3_out[6]), .in7(and_3_out[7]), .out(out_10), .en_in(in_2),
    .gs(priority_encoder_1_gs), .en_out(out_9));
  Register #(.width(4)) s1 (.D(adder_2_out), .en(and_4_out), .Q(s1_q), .clk(and_1_out), .clr(Reset_out));
  Register #(.width(4)) s2 (.D(adder_1_out), .en(and_5_out), .Q(s2_q), .clk(and_1_out), .clr(Reset_out));
  Register #(.width(4)) s3 (.D(adder_3_out), .en(and_6_out), .Q(s3_q), .clk(and_1_out), .clr(Reset_out));
  Adder #(.width(4)) adder_1 (.a(s2_q), .b(in_6), .out(adder_1_out));  // open: cin, cout
  assign not_2_out = ~decoder_1_out0;  // NOT_Gate not_2, 8 bits wide
  Multiplexer #(.select(3)) multiplexer_1 (
    .in0(and_3_out[0]), .in1(and_3_out[1]), .in2(and_3_out[2]), .in3(and_3_out[3]), .in4(and_3_out[4]),
    .in5(and_3_out[5]), .in6(and_3_out[6]), .in7(and_3_out[7]), .out(multiplexer_1_out), .sel(out_10),
    .en(in_2));
  Comparator #(.width(4), .mode("unsigned")) comparator_1 (
    .a(s1_q), .b(in_3), .gt(comparator_1_gt), .eq(comparator_1_eq));  // open: lt
  Adder #(.width(4)) adder_2 (.a(s1_q), .b(in_4), .out(adder_2_out));  // open: cin, cout
  Comparator #(.width(4), .mode("unsigned")) comparator_2 (
    .a(s2_q), .b(in_5), .gt(comparator_2_gt), .eq(comparator_2_eq));  // open: lt
  Comparator #(.width(4), .mode("unsigned")) comparator_3 (
    .a(s3_q), .b(in_7), .gt(comparator_3_gt), .eq(comparator_3_eq));  // open: lt
  Adder #(.width(4)) adder_3 (.a(s3_q), .b(in_8), .out(adder_3_out));  // open: cin, cout
  and and_7 (and_7_out, priority_encoder_1_gs, multiplexer_1_out);
  or or_4 (or_4_out, comparator_1_gt, comparator_1_eq);
  or or_5 (or_5_out, comparator_2_gt, comparator_2_eq);
  or or_6 (or_6_out, comparator_3_gt, comparator_3_eq);
  assign and_8_out = not_2_out & and_3_out;  // AND_Gate and_8, 8 bits wide
  Hex_Digit_Display hex_digit_display_1 (.value(s1_q));  // open: dp
  not not_3 (not_3_out, or_4_out);
  _8_input_flip_flop u_8_input_flip_flop_2 (
    .\input (and_8_out), .clk(and_1_out), .clear__1_to_clear(Reset_out),
    .\output (n8_input_flip_flop_2_output));
  Hex_Digit_Display hex_digit_display_2 (.value(s3_q));  // open: dp
  Hex_Digit_Display hex_digit_display_3 (.value(s2_q));  // open: dp
  comparator_server comparator_server_1 (
    .Server_1_counter(s1_q), .Server_2_counter(s2_q), .Server_3_counter(s3_q),
    .Server_1(comparator_server_1_server_1), .Server_2(comparator_server_1_server_2),
    .Server_3(comparator_server_1_server_3));
  LED Overload (.in(and_9_out));
  and and_9 (and_9_out, or_6_out, or_5_out, or_4_out);
  and and_10 (and_10_out, not_3_out, comparator_server_1_server_1);
  LED Load_rebalancing_trriger (.in(or_7_out));
  or or_7 (or_7_out, or_4_out, or_5_out, or_6_out);

  // Notes on the sheet:
  //   Dynamic Load Balancer circuit
  //   Instructions:
  //   1.Click on the  "Reset button to reset the circuit
  //   3.Click on the clock button (clock pulse) to assign each task
  //   i.Red LED indicates tasks assigned to server-1
  //   ii.Blue LED indicates tasks assigned to server-2
  //   iii.Pink LED indicates task assigned to server-3
  //   6.Load rebalancing trrigers if any server reaches threshold 
  //   2.Put the inputs in the input queue (1 if task to be alloted 0 to be neglected)
  //   4. Check the LED'S to find which task is assigned to which server
  //   5.Check the Overload LED which indicates all servers have reached the threshold
endmodule

// 8-Input flipflop
module _8_input_flip_flop (
  input  [7:0] \input ,
  input  clk,
  input  clear__1_to_clear,
  output [7:0] \output 
);

  D_Flip_Flop d_ff_1 (.clk(clk), .D(\input [0]), .Q(\output [0]), .reset(clear__1_to_clear));  // open: Qn, preset, en
  D_Flip_Flop d_ff_2 (.clk(clk), .D(\input [1]), .Q(\output [1]), .reset(clear__1_to_clear));  // open: Qn, preset, en
  D_Flip_Flop d_ff_3 (.clk(clk), .D(\input [2]), .Q(\output [2]), .reset(clear__1_to_clear));  // open: Qn, preset, en
  D_Flip_Flop d_ff_4 (.clk(clk), .D(\input [3]), .Q(\output [3]), .reset(clear__1_to_clear));  // open: Qn, preset, en
  D_Flip_Flop d_ff_5 (.clk(clk), .D(\input [4]), .Q(\output [4]), .reset(clear__1_to_clear));  // open: Qn, preset, en
  D_Flip_Flop d_ff_6 (.clk(clk), .D(\input [5]), .Q(\output [5]), .reset(clear__1_to_clear));  // open: Qn, preset, en
  D_Flip_Flop d_ff_7 (.clk(clk), .D(\input [6]), .Q(\output [6]), .reset(clear__1_to_clear));  // open: Qn, preset, en
  D_Flip_Flop d_ff_8 (.clk(clk), .D(\input [7]), .Q(\output [7]), .reset(clear__1_to_clear));  // open: Qn, preset, en

  // Notes on the sheet:
  //   8-Input Flip Flop
  //   Description:
  //   -> This 8-input Flip Flop is constructed to store 8 inputs at a time
endmodule
