// Logisim project mini_project_hardware_design.circ as structural Verilog: 1 circuit, main circuit main
module main (
  input  [3:0] Input_tasks,
  output [1:0] server_1,
  output [1:0] server_2
);

  wire and_1_out, and_2_out, clk_out, clr_out, comparator_1_gt, not_1_out, rgyhdsa_carry;
  wire [1:0] rgyhdsa_q;
  wire [3:0] shifter_1_out;

  Counter #(.width(2), .max('h3), .ongoal("load")) rgyhdsa (
    .Q(rgyhdsa_q), .carry(rgyhdsa_carry), .clk(clk_out), .clr(clr_out));  // open: load, D, count
  Button clk (.out(clk_out));
  Button clr (.out(clr_out));
  Shifter #(.width(4), .shift("lr")) shifter_1 (.in(Input_tasks), .\dist (rgyhdsa_q), .out(shifter_1_out));
  not not_1 (not_1_out, comparator_1_gt);
  and and_1 (and_1_out, shifter_1_out[0], comparator_1_gt);
  and and_2 (and_2_out, shifter_1_out[0], not_1_out);
  Counter #(.width(2), .max('h3), .ongoal("stay"), .trigger("falling")) server1 (
    .count(and_2_out), .Q(server_1), .clk(clk_out), .clr(clr_out));  // open: load, D, carry
  Counter #(.width(2), .max('h3), .ongoal("stay"), .trigger("falling")) server2 (
    .count(and_1_out), .Q(server_2), .clk(clk_out), .clr(clr_out));  // open: load, D, carry
  LED led_1 (.in(rgyhdsa_carry));
  Comparator #(.width(2), .mode("unsigned")) comparator_1 (
    .a(server_1), .b(server_2), .gt(comparator_1_gt));  // open: eq, lt

  // Notes on the sheet:
  //   counter
  //   server-1
  //   server-2
  //   comparator
  //   output no of tasks assigned to each server
  //   indicates next clk pulse is last
endmodule
